# Fritzing sketch esquema fritzing despertadorSolar (saved by Fritzing 1.0.4)
breadboards: 1

parts:
  LCD2004-I2C1 = LCD2004-I2C
  Componente1 = Arduino Nano (Rev3.0)

nets:
  GND: LCD2004-I2C1.GND, Componente1.GND
  VCC: LCD2004-I2C1.VCC, Componente1.VIN
  N1: LCD2004-I2C1.SDA, Componente1.A5
  N2: LCD2004-I2C1.SCL, Componente1.A4

custom parts:
  LCD2004-I2C: A standard character display with 4x20 characters. Comes in many colors with LCM2004 IIC attached.
